# Fritzing sketch circuit (saved by Fritzing 0.9.4)
circuit board: 8.46667cm x 5.64444cm
breadboards: 1

parts:
  Part1 = Arduino Uno (Rev3) - ICSP
  LED1 = RGB LED (com. cathode, rbg) [package="5 mm [THT]"]

nets:
  N1: Part1.GND, LED1.common_cathode
  N2: Part1.D9_PWM, LED1.red_anode
  N3: Part1.D10_PWM/SS, LED1.green_anode
  N4: Part1.D11_PWM/MOSI, LED1.blue_anode
